// Logisim project project.circ as structural Verilog: 8 circuits, main circuit projectCPU
module projectCPU (
  input  Write_Read_0_1,
  input  _4_bit_data_input,
  input  in_3,
  input  in_4,
  input  in_5
);

  wire a5ram_1_lsbout, a5ram_1_msbout, a5ram_1_out_11, a5ram_1_out_12, a6alu_1_lsbout, a6alu_1_msbout,
       a6alu_1_negative, a6alu_1_out_15, a6alu_1_out_16, a6alu_1_overflow, a6alu_1_zero, and_1_out,
       and_2_out, and_3_out, and_4_out, and_5_out, and_6_out, and_7_out, and_8_out, and_9_out, and_10_out,
       and_11_out, and_12_out, and_13_out, and_14_out, and_15_out, and_16_out, and_17_out, and_18_out,
       and_19_out, and_20_out, and_21_out, and_22_out, and_23_out, and_24_out, and_25_out, and_26_out,
       and_27_out, and_28_out, and_29_out, and_30_out, and_31_out, and_32_out, and_33_out, and_34_out,
       and_35_out, and_36_out, and_37_out, and_38_out, and_39_out, and_40_out, and_41_out, and_42_out,
       and_43_out, and_44_out, and_45_out, and_46_out, and_47_out, and_48_out, and_49_out, and_50_out,
       and_51_out, and_52_out, and_53_out, and_54_out, and_55_out, and_56_out, and_57_out, and_58_out,
       and_59_out, and_60_out, and_61_out, clock_1_out, d_ff_1_q, d_ff_2_q, d_ff_3_q, d_ff_4_q,
       Dataram_lsbout, Dataram_msbout, Dataram_out_9, Dataram_out_10, decoder_1_out1, decoder_2_out0,
       decoder_2_out1, decoder_3_out0, decoder_3_out1, decoder_4_out0, decoder_4_out1, decoder_5_out0,
       decoder_5_out1, decoder_6_out0, decoder_6_out1, decoder_7_out0, decoder_8_out0, decoder_8_out1,
       decoder_9_out0, decoder_9_out1, halfadder_1_carryout, halfadder_1_sum, halfadder_2_carryout,
       halfadder_2_sum, halfadder_3_carryout, halfadder_3_sum, halfadder_4_carryout, halfadder_4_sum,
       multiplexer_1_out, multiplexer_2_out, multiplexer_3_out, multiplexer_4_out, multiplexer_5_out,
       multiplexer_6_out, multiplexer_7_out, multiplexer_8_out, multiplexer_9_out, multiplexer_10_out,
       multiplexer_11_out, multiplexer_12_out, not_1_out, not_2_out, not_3_out, not_4_out, not_5_out,
       not_6_out, not_7_out, not_8_out, not_9_out, not_10_out, or_1_out, or_2_out, or_3_out, or_4_out,
       or_5_out, or_6_out, or_8_out, or_9_out, or_10_out, or_11_out, or_12_out, or_13_out, or_14_out,
       or_15_out, or_16_out, or_17_out, or_18_out, or_19_out, or_20_out, or_21_out, or_22_out, or_23_out,
       or_24_out, or_25_out, or_26_out, or_27_out, or_28_out, or_29_out, or_30_out, or_31_out, or_32_out,
       or_33_out, or_34_out, R0_lsbout, R0_msbout, R0_out_8, R0_out_9, R1_lsbout, R1_msbout, R1_out_8,
       R1_out_9, xor_1_out, xor_2_out;

  D_Flip_Flop d_ff_1 (.D(halfadder_1_sum), .clk(and_1_out), .Q(d_ff_1_q));  // open: Qn, preset, reset
  // Probe on halfadder_1_carryout
  HalfAdder halfadder_1 (
    .CarryIn(halfadder_2_carryout), .Input1(d_ff_1_q), .Input2(1'b0), .Sum(halfadder_1_sum),
    .CarryOut(halfadder_1_carryout));
  D_Flip_Flop d_ff_2 (.D(halfadder_2_sum), .clk(and_1_out), .Q(d_ff_2_q));  // open: Qn, preset, reset
  HalfAdder halfadder_2 (
    .CarryIn(halfadder_3_carryout), .Input1(d_ff_2_q), .Input2(1'b0), .Sum(halfadder_2_sum),
    .CarryOut(halfadder_2_carryout));
  Clock clock_1 (.out(clock_1_out));
  D_Flip_Flop d_ff_3 (.D(halfadder_3_sum), .clk(and_1_out), .Q(d_ff_3_q));  // open: Qn, preset, reset
  HalfAdder halfadder_3 (
    .CarryIn(halfadder_4_carryout), .Input1(d_ff_3_q), .Input2(1'b0), .Sum(halfadder_3_sum),
    .CarryOut(halfadder_3_carryout));
  not not_1 (not_1_out, and_2_out);
  and and_1 (and_1_out, not_1_out, clock_1_out);
  D_Flip_Flop d_ff_4 (.D(1'b1), .clk(and_1_out), .Q(d_ff_4_q));  // open: Qn, preset, reset
  // Probe on halfadder_4_sum
  HalfAdder halfadder_4 (
    .CarryIn(1'b0), .Input1(d_ff_4_q), .Input2(1'b1), .Sum(halfadder_4_sum), .CarryOut(halfadder_4_carryout));
  and and_2 (and_2_out, and_3_out, and_4_out);
  and and_3 (and_3_out, a5ram_1_out_11, a5ram_1_lsbout);
  and and_4 (and_4_out, a5ram_1_msbout, a5ram_1_out_12);
  A5ram a5ram_1 (
    .Clock(and_1_out), .MSBaddy(halfadder_1_sum), .in_3(halfadder_2_sum), .LSBaddy(halfadder_3_sum),
    .ModeInput(Write_Read_0_1), .MSBin(_4_bit_data_input), .in_7(in_3), .in_8(in_4), .LSBin(in_5),
    .MSBout(a5ram_1_msbout), .out_11(a5ram_1_out_11), .out_12(a5ram_1_out_12), .LSBout(a5ram_1_lsbout));
  not not_2 (not_2_out, a5ram_1_msbout);
  not not_3 (not_3_out, a5ram_1_out_11);
  not not_4 (not_4_out, a5ram_1_msbout);
  not not_5 (not_5_out, a5ram_1_out_11);
  and and_5 (and_5_out, a5ram_1_lsbout, or_1_out);
  and and_6 (and_6_out, not_2_out, not_3_out);
  and and_7 (and_7_out, not_4_out, a5ram_1_out_11);
  and and_8 (and_8_out, a5ram_1_msbout, not_5_out);
  and and_9 (and_9_out, a5ram_1_msbout, a5ram_1_out_11);
  Decoder decoder_1 (.out1(decoder_1_out1), .sel(a5ram_1_out_12));  // open: out0, en
  and and_10 (and_10_out, or_1_out, a5ram_1_out_12);
  not not_6 (not_6_out, and_8_out);
  and and_11 (and_11_out, not_6_out, and_9_out);
  Decoder decoder_2 (.out0(decoder_2_out0), .out1(decoder_2_out1), .sel(a5ram_1_out_12));  // open: en
  or or_1 (or_1_out, and_8_out, and_9_out);
  Decoder decoder_3 (.out0(decoder_3_out0), .out1(decoder_3_out1), .sel(a5ram_1_out_12));  // open: en
  Decoder decoder_4 (.out0(decoder_4_out0), .out1(decoder_4_out1), .sel(and_10_out));  // open: en
  Decoder decoder_5 (.out0(decoder_5_out0), .out1(decoder_5_out1), .sel(and_10_out));  // open: en
  Decoder decoder_6 (.out0(decoder_6_out0), .out1(decoder_6_out1), .sel(and_5_out));  // open: en
  and and_12 (and_12_out, and_6_out, decoder_2_out0);
  Multiplexer #(.enable("false")) multiplexer_1 (
    .in0(and_8_out), .in1(and_9_out), .out(multiplexer_1_out), .sel(and_11_out));
  Decoder decoder_7 (.out0(decoder_7_out0), .sel(a5ram_1_out_12));  // open: out1, en
  not not_7 (not_7_out, and_12_out);
  and and_13 (and_13_out, and_7_out, decoder_2_out0);
  or or_2 (or_2_out, multiplexer_2_out, or_6_out);
  and and_14 (and_14_out, decoder_2_out1, and_7_out);
  and and_15 (and_15_out, and_6_out, decoder_2_out1);
  not not_8 (not_8_out, and_14_out);
  or or_3 (or_3_out, decoder_1_out1, or_6_out);
  and and_16 (and_16_out, or_1_out, decoder_3_out0);
  and and_17 (and_17_out, or_1_out, decoder_3_out1);
  and and_18 (and_18_out, or_1_out, decoder_6_out0);
  or or_4 (or_4_out, and_54_out, and_30_out);
  or or_5 (or_5_out, decoder_7_out0, or_6_out);
  and and_19 (and_19_out, not_7_out, and_13_out);
  Multiplexer #(.enable("false")) multiplexer_2 (
    .in0(and_14_out), .in1(and_15_out), .out(multiplexer_2_out), .sel(and_20_out));
  and and_20 (and_20_out, and_15_out, not_8_out);
  or or_6 (or_6_out, and_16_out, and_18_out);
  and and_21 (and_21_out, or_1_out, decoder_6_out1);
  or or_7 (or_6_out, and_21_out, and_17_out);
  or or_8 (or_8_out, and_55_out, and_33_out);
  or or_9 (or_9_out, and_56_out, and_35_out);
  or or_10 (or_10_out, and_57_out, and_42_out);
  or or_11 (or_11_out, and_36_out, and_58_out);
  or or_12 (or_12_out, and_38_out, and_59_out);
  or or_13 (or_13_out, and_43_out, and_60_out);
  or or_14 (or_14_out, and_47_out, and_61_out);
  or or_15 (or_15_out, multiplexer_3_out, or_6_out);
  Multiplexer #(.enable("false")) multiplexer_3 (
    .in0(and_13_out), .in1(and_12_out), .out(multiplexer_3_out), .sel(and_19_out));
  or or_16 (or_16_out, and_13_out, and_14_out);
  or or_17 (or_17_out, and_12_out, and_15_out);
  Decoder decoder_8 (.out0(decoder_8_out0), .out1(decoder_8_out1), .sel(a5ram_1_out_12), .en(or_1_out));
  Decoder decoder_9 (.out0(decoder_9_out0), .out1(decoder_9_out1), .sel(and_5_out), .en(or_1_out));
  NibbleRegister R0 (
    .clock(and_1_out), .Read1Write0(xor_1_out), .MSBin(or_10_out), .in_4(or_9_out), .in_5(or_8_out),
    .LSBin(or_4_out), .MSBout(R0_msbout), .out_8(R0_out_8), .out_9(R0_out_9), .LSBout(R0_lsbout));
  Multiplexer #(.enable("false")) multiplexer_4 (
    .in0(or_17_out), .in1(or_16_out), .out(multiplexer_4_out), .sel(and_22_out));
  and and_22 (and_22_out, or_16_out, or_17_out);
  NibbleRegister R1 (
    .clock(and_1_out), .Read1Write0(xor_2_out), .MSBin(or_14_out), .in_4(or_13_out), .in_5(or_12_out),
    .LSBin(or_11_out), .MSBout(R1_msbout), .out_8(R1_out_8), .out_9(R1_out_9), .LSBout(R1_lsbout));
  Multiplexer #(.enable("false")) multiplexer_5 (
    .in0(R1_msbout), .in1(or_3_out), .out(multiplexer_5_out), .sel(not_9_out));
  not not_9 (not_9_out, or_3_out);
  xor xor_1 (xor_1_out, or_15_out, and_39_out);
  Multiplexer #(.enable("false")) multiplexer_6 (
    .in0(or_5_out), .in1(R0_msbout), .out(multiplexer_6_out), .sel(or_5_out));
  Multiplexer #(.enable("false")) multiplexer_7 (
    .in0(or_5_out), .in1(R0_out_8), .out(multiplexer_7_out), .sel(or_5_out));
  Multiplexer #(.enable("false")) multiplexer_8 (
    .in0(or_5_out), .in1(R0_out_9), .out(multiplexer_8_out), .sel(or_5_out));
  Multiplexer #(.enable("false")) multiplexer_9 (
    .in0(or_5_out), .in1(R0_lsbout), .out(multiplexer_9_out), .sel(or_5_out));
  Multiplexer #(.enable("false")) multiplexer_10 (
    .in0(R1_out_8), .in1(or_3_out), .out(multiplexer_10_out), .sel(not_9_out));
  Multiplexer #(.enable("false")) multiplexer_11 (
    .in0(R1_lsbout), .in1(or_3_out), .out(multiplexer_11_out), .sel(not_9_out));
  and and_23 (and_23_out, multiplexer_11_out, decoder_8_out1);
  and and_24 (and_24_out, multiplexer_8_out, decoder_8_out0);
  and and_25 (and_25_out, multiplexer_9_out, decoder_8_out0);
  and and_26 (and_26_out, multiplexer_6_out, decoder_9_out0);
  and and_27 (and_27_out, multiplexer_7_out, decoder_9_out0);
  and and_28 (and_28_out, multiplexer_8_out, decoder_9_out0);
  and and_29 (and_29_out, multiplexer_9_out, decoder_9_out0);
  and and_30 (and_30_out, Dataram_lsbout, decoder_4_out0);
  Multiplexer #(.enable("false")) multiplexer_12 (
    .in0(R1_out_9), .in1(or_3_out), .out(multiplexer_12_out), .sel(not_9_out));
  and and_31 (and_31_out, multiplexer_12_out, decoder_8_out1);
  and and_32 (and_32_out, multiplexer_7_out, decoder_8_out0);
  and and_33 (and_33_out, Dataram_out_10, decoder_4_out0);
  xor xor_2 (xor_2_out, or_2_out, and_48_out);
  and and_34 (and_34_out, multiplexer_6_out, decoder_8_out0);
  and and_35 (and_35_out, Dataram_out_9, decoder_4_out0);
  and and_36 (and_36_out, Dataram_lsbout, decoder_4_out1);
  or or_18 (or_18_out, multiplexer_6_out, multiplexer_5_out);
  or or_19 (or_19_out, multiplexer_7_out, multiplexer_10_out);
  or or_20 (or_20_out, multiplexer_8_out, multiplexer_12_out);
  or or_21 (or_21_out, multiplexer_9_out, multiplexer_11_out);
  and and_37 (and_37_out, multiplexer_10_out, decoder_8_out1);
  and and_38 (and_38_out, Dataram_out_10, decoder_4_out1);
  and and_39 (and_39_out, not_10_out, or_31_out);
  and and_40 (and_40_out, multiplexer_5_out, decoder_8_out1);
  and and_41 (and_41_out, multiplexer_11_out, decoder_9_out1);
  and and_42 (and_42_out, Dataram_msbout, decoder_4_out0);
  and and_43 (and_43_out, Dataram_out_9, decoder_4_out1);
  or or_22 (or_22_out, and_6_out, and_7_out);
  and and_44 (and_44_out, multiplexer_5_out, decoder_9_out1);
  and and_45 (and_45_out, multiplexer_10_out, decoder_9_out1);
  and and_46 (and_46_out, multiplexer_12_out, decoder_9_out1);
  and and_47 (and_47_out, Dataram_msbout, decoder_4_out1);
  not not_10 (not_10_out, a5ram_1_out_12);
  and and_48 (and_48_out, a5ram_1_out_12, or_31_out);
  or or_23 (or_23_out, and_40_out, and_34_out);
  or or_24 (or_24_out, and_37_out, and_32_out);
  or or_25 (or_25_out, and_31_out, and_24_out);
  or or_26 (or_26_out, and_23_out, and_25_out);
  or or_27 (or_27_out, and_44_out, and_26_out);
  or or_28 (or_28_out, and_45_out, and_27_out);
  or or_29 (or_29_out, and_46_out, and_28_out);
  or or_30 (or_30_out, and_41_out, and_29_out);
  and and_49 (and_49_out, or_1_out, a6alu_1_zero);
  and and_50 (and_50_out, or_18_out, or_22_out);
  and and_51 (and_51_out, or_19_out, or_22_out);
  and and_52 (and_52_out, or_20_out, or_22_out);
  and and_53 (and_53_out, or_21_out, or_22_out);
  or or_31 (or_31_out, and_49_out, or_32_out);
  or or_32 (or_32_out, or_33_out, or_34_out);
  or or_33 (or_33_out, a6alu_1_msbout, a6alu_1_out_16);
  or or_34 (or_34_out, a6alu_1_out_15, a6alu_1_lsbout);
  and and_54 (and_54_out, a6alu_1_lsbout, decoder_5_out0);
  and and_55 (and_55_out, a6alu_1_out_16, decoder_5_out0);
  // Probe on a6alu_1_zero
  A6alu a6alu_1 (
    .MSBunsignIn(or_23_out), .in_2(or_24_out), .in_3(or_25_out), .LSBunsignIn(or_26_out),
    .MSBsignIn(or_27_out), .in_6(or_28_out), .in_7(or_29_out), .LSBsignOut(or_30_out), .Clock(and_1_out),
    .add0sub1(multiplexer_1_out), .Zero(a6alu_1_zero), .Negative(a6alu_1_negative),
    .Overflow(a6alu_1_overflow), .MSBout(a6alu_1_msbout), .out_15(a6alu_1_out_15), .out_16(a6alu_1_out_16),
    .LSBout(a6alu_1_lsbout));
  and and_56 (and_56_out, a6alu_1_out_15, decoder_5_out0);
  and and_57 (and_57_out, a6alu_1_msbout, decoder_5_out0);
  and and_58 (and_58_out, a6alu_1_lsbout, decoder_5_out1);
  and and_59 (and_59_out, a6alu_1_out_16, decoder_5_out1);
  and and_60 (and_60_out, a6alu_1_out_15, decoder_5_out1);
  and and_61 (and_61_out, a6alu_1_msbout, decoder_5_out1);
  // Probe on a6alu_1_negative
  // Probe on a6alu_1_overflow
  NibbleRam Dataram (
    .CLOCK(and_1_out), .bit0or1(a5ram_1_lsbout), .READ1WRITE0(multiplexer_4_out), .MSBin(and_50_out),
    .in_5(and_51_out), .in_6(and_52_out), .LSBin(and_53_out), .MSBout(Dataram_msbout), .out_9(Dataram_out_9),
    .out_10(Dataram_out_10), .LSBout(Dataram_lsbout));

  // Notes on the sheet:
  //   MSB ram
  //   This simple adder is made so that the 3 rightmost bits are used as Address inputs and the LSB is used as a 2 clock cycle buffer for the 000 instruction to run before incrementing to the next address
  //   LSBram
  //   Having this LSB in the buffer makes it so that every 2 clock cycles or adding 1 twice will update the actual LSB checked in the address therefore allowing 1 update per 2 ticks 
  //   HALT only when instruction is 1111 stops clock tick
  //   add1buffer
  //   dataram
  //   load
  //   save
  //   register
  //   add
  //   sub
  //   register selector for add sub first
  //   register for add sub second
  //   Only this register can be signed
  //   operation first term
  //   operation second term
  //   R1
  //   MSB
  //   are we doing add/sub
  //   Deternines sol out
  //   ALWAYS UNSIGNED
  //   SIGNED REGISTER IF SUB
  //   MSB
  //   R0
  //   load R0
  //   SAVE r1
  //   load R1
  //   decideRambit
  //   R0
  //   R0
  //   LSB
  //   MSB
  //   save r0
  //   add/sub
  //   R1
  //   R1
  //   R0
  //   R1
  //   0 for load 1 for save
  //   R0read write toggle
  //   MSB R1
  //   LSB R1
  //   LSBr0
  //   R0
  //   If either saves are toggled then swap dataRam to write
  //   If this is toggled,load is active and we swap dataRam to read
  //   MSBr0
  //   LSB
  //   R0msb
  //   R0lsb
  //   R1msb
  //   LSB
  //   MSB
  //   MSB
  //   LSB
  //   R1 read write Toggle
  //   R1lsb
  //   0/1 bit selector
  //   R0 unsignOUT
  //   MSB
  //   LSB
  //   R1 load
  //   R0
  //   R1 unsign out
  //   MSB
  //   LSB
  //   MSB
  //   MSB 
  //   LSB
  //   R1
  //   DataRAM passes only on L/S inst.
  //   LSB
  //   MSB
  //   LSB
  //   MSB
  //   R0 out
  //   R1 out
  //   LSB
  //   MSB
endmodule

module NibbleRegister (
  input  clock,
  input  Read1Write0,
  input  MSBin,
  input  in_4,
  input  in_5,
  input  LSBin,
  output MSBout,
  output out_8,
  output out_9,
  output LSBout
);

  wire and_1_out, d_ff_1_q, d_ff_2_q, d_ff_3_q, d_ff_4_q, not_1_out;

  and and_1 (and_1_out, clock, not_1_out);
  not not_1 (not_1_out, Read1Write0);
  and and_2 (MSBout, Read1Write0, d_ff_1_q);
  D_Flip_Flop d_ff_1 (.D(MSBin), .clk(and_1_out), .Q(d_ff_1_q));  // open: Qn, preset, reset
  D_Flip_Flop d_ff_2 (.D(in_4), .clk(and_1_out), .Q(d_ff_2_q));  // open: Qn, preset, reset
  and and_3 (out_8, Read1Write0, d_ff_2_q);
  and and_4 (out_9, Read1Write0, d_ff_3_q);
  D_Flip_Flop d_ff_3 (.D(in_5), .clk(and_1_out), .Q(d_ff_3_q));  // open: Qn, preset, reset
  D_Flip_Flop d_ff_4 (.D(LSBin), .clk(and_1_out), .Q(d_ff_4_q));  // open: Qn, preset, reset
  and and_5 (LSBout, Read1Write0, d_ff_4_q);
endmodule

module NibbleRam (
  input  CLOCK,
  input  bit0or1,
  input  READ1WRITE0,
  input  MSBin,
  input  in_5,
  input  in_6,
  input  LSBin,
  output MSBout,
  output out_9,
  output out_10,
  output LSBout
);

  wire and_1_out, and_2_out, and_3_out, and_4_out, and_5_out, and_6_out, and_7_out, and_8_out, and_9_out,
       and_10_out, and_11_out, and_12_out, and_13_out, and_14_out, and_15_out, and_16_out, and_17_out,
       and_18_out, and_19_out, and_20_out, and_21_out, decoder_1_out0, decoder_1_out1, decoder_2_out0,
       decoder_2_out1, nibbleregister_1_lsbout, nibbleregister_1_msbout, nibbleregister_1_out_8,
       nibbleregister_1_out_9, nibbleregister_2_lsbout, nibbleregister_2_msbout, nibbleregister_2_out_8,
       nibbleregister_2_out_9, not_1_out;

  and and_1 (and_1_out, and_12_out, decoder_1_out0);
  not not_1 (not_1_out, READ1WRITE0);
  and and_2 (and_2_out, decoder_1_out0, and_6_out);
  Decoder decoder_1 (.out0(decoder_1_out0), .out1(decoder_1_out1), .sel(bit0or1));  // open: en
  Decoder decoder_2 (.out0(decoder_2_out0), .out1(decoder_2_out1), .sel(bit0or1));  // open: en
  and and_3 (and_3_out, not_1_out, CLOCK);
  and and_4 (and_4_out, decoder_1_out0, and_8_out);
  and and_5 (and_5_out, decoder_1_out0, and_9_out);
  and and_6 (and_6_out, not_1_out, MSBin);
  and and_7 (and_7_out, decoder_2_out0, nibbleregister_1_msbout);
  and and_8 (and_8_out, not_1_out, in_5);
  and and_9 (and_9_out, not_1_out, in_6);
  or or_1 (MSBout, and_7_out, and_17_out);
  and and_10 (and_10_out, decoder_2_out0, nibbleregister_1_out_8);
  and and_11 (and_11_out, decoder_2_out0, nibbleregister_1_out_9);
  NibbleRegister nibbleregister_1 (
    .clock(and_3_out), .Read1Write0(READ1WRITE0), .MSBin(and_2_out), .in_4(and_4_out), .in_5(and_5_out),
    .LSBin(and_1_out), .MSBout(nibbleregister_1_msbout), .out_8(nibbleregister_1_out_8),
    .out_9(nibbleregister_1_out_9), .LSBout(nibbleregister_1_lsbout));
  and and_12 (and_12_out, not_1_out, LSBin);
  or or_2 (out_9, and_10_out, and_19_out);
  and and_13 (and_13_out, decoder_2_out0, nibbleregister_1_lsbout);
  and and_14 (and_14_out, decoder_1_out1, and_6_out);
  or or_3 (out_10, and_11_out, and_20_out);
  and and_15 (and_15_out, decoder_1_out1, and_8_out);
  or or_4 (LSBout, and_13_out, and_21_out);
  and and_16 (and_16_out, decoder_1_out1, and_9_out);
  and and_17 (and_17_out, decoder_2_out1, nibbleregister_2_msbout);
  NibbleRegister nibbleregister_2 (
    .clock(and_3_out), .Read1Write0(READ1WRITE0), .MSBin(and_14_out), .in_4(and_15_out), .in_5(and_16_out),
    .LSBin(and_18_out), .MSBout(nibbleregister_2_msbout), .out_8(nibbleregister_2_out_8),
    .out_9(nibbleregister_2_out_9), .LSBout(nibbleregister_2_lsbout));
  and and_18 (and_18_out, decoder_1_out1, and_12_out);
  and and_19 (and_19_out, decoder_2_out1, nibbleregister_2_out_8);
  and and_20 (and_20_out, decoder_2_out1, nibbleregister_2_out_9);
  and and_21 (and_21_out, decoder_2_out1, nibbleregister_2_lsbout);
endmodule

module A6alu (
  input  MSBunsignIn,
  input  in_2,
  input  in_3,
  input  LSBunsignIn,
  input  MSBsignIn,
  input  in_6,
  input  in_7,
  input  LSBsignOut,
  input  Clock,
  input  add0sub1,
  output Zero,
  output Negative,
  output Overflow,
  output MSBout,
  output out_15,
  output out_16,
  output LSBout
);

  wire a6adder_1_c, a6adder_2_c, a6adder_3_c, and_1_out, and_2_out, and_3_out, and_4_out, and_5_out,
       and_6_out, and_7_out, and_8_out, and_9_out, and_10_out, and_11_out, and_12_out, and_13_out,
       and_14_out, and_15_out, and_16_out, and_17_out, and_18_out, and_19_out, and_20_out, and_21_out,
       and_22_out, and_24_out, and_25_out, and_26_out, and_27_out, Neg_out, not_1_out, not_2_out, not_3_out,
       not_4_out, not_5_out, not_6_out, not_7_out, not_8_out, not_9_out, not_10_out, not_11_out, not_12_out,
       not_13_out, not_14_out, not_15_out, or_1_out, or_2_out, or_3_out, or_4_out, or_5_out, Pos_out,
       xor_2_out, xor_3_out, xor_4_out, xor_5_out;

  not not_1 (not_1_out, add0sub1);
  and and_1 (and_1_out, MSBunsignIn, Clock);
  and and_2 (and_2_out, in_2, Clock);
  and and_3 (and_3_out, in_3, Clock);
  A6adder a6adder_1 (.A(or_1_out), .B(and_1_out), .Carry(a6adder_2_c), .C(a6adder_1_c), .Sum(MSBout));
  and and_4 (and_4_out, LSBunsignIn, Clock);
  A6adder a6adder_2 (.A(or_2_out), .B(and_2_out), .Carry(a6adder_3_c), .C(a6adder_2_c), .Sum(out_15));
  or or_1 (or_1_out, xor_2_out, and_6_out);
  A6adder a6adder_3 (.A(or_3_out), .B(and_3_out), .Carry(and_5_out), .C(a6adder_3_c), .Sum(out_16));
  or or_2 (or_2_out, xor_3_out, and_8_out);
  or or_3 (or_3_out, xor_4_out, and_9_out);
  and and_5 (and_5_out, and_4_out, or_4_out);
  xor xor_1 (LSBout, and_4_out, or_4_out);
  and and_6 (and_6_out, and_12_out, not_1_out);
  and and_7 (and_7_out, not_6_out, and_10_out);
  or or_4 (or_4_out, xor_5_out, and_14_out);
  not not_2 (not_2_out, LSBout);
  not not_3 (not_3_out, out_16);
  not not_4 (not_4_out, out_15);
  not not_5 (not_5_out, MSBout);
  and and_8 (and_8_out, and_13_out, not_1_out);
  and and_9 (and_9_out, and_17_out, not_1_out);
  xor xor_2 (xor_2_out, not_6_out, and_10_out);
  and and_10 (and_10_out, not_10_out, and_16_out);
  and and_11 (and_11_out, not_2_out, not_3_out, not_4_out, not_5_out);
  and and_12 (and_12_out, MSBsignIn, Clock);
  and and_13 (and_13_out, in_6, Clock);
  and and_14 (and_14_out, and_18_out, not_1_out);
  and and_15 (and_15_out, and_12_out, add0sub1);
  not not_6 (not_6_out, and_15_out);
  xor xor_3 (xor_3_out, not_10_out, and_16_out);
  and and_16 (and_16_out, not_11_out, and_22_out);
  not not_7 (not_7_out, or_1_out);
  not not_8 (not_8_out, and_1_out);
  not not_9 (not_9_out, or_1_out);
  and and_17 (and_17_out, in_7, Clock);
  and and_18 (and_18_out, LSBsignOut, Clock);
  and and_19 (and_19_out, and_13_out, add0sub1);
  and and_20 (and_20_out, and_17_out, add0sub1);
  and and_21 (and_21_out, and_18_out, add0sub1);
  not not_10 (not_10_out, and_19_out);
  not not_11 (not_11_out, and_20_out);
  not not_12 (not_12_out, and_21_out);
  xor xor_4 (xor_4_out, not_11_out, and_22_out);
  and and_22 (and_22_out, not_12_out, 1'b1);
  and Neg (Neg_out, or_1_out, and_1_out);
  and Pos (Pos_out, not_7_out, not_8_out);
  and and_23 (Zero, and_11_out, Clock);
  xor xor_5 (xor_5_out, not_12_out, 1'b1);
  and and_24 (and_24_out, MSBout, Neg_out);
  and and_25 (and_25_out, Pos_out, MSBout);
  and and_26 (and_26_out, not_13_out, not_9_out, a6adder_1_c);
  not not_13 (not_13_out, add0sub1);
  not not_14 (not_14_out, a6adder_1_c);
  and and_27 (and_27_out, and_24_out, not_14_out);
  or or_5 (or_5_out, and_26_out, and_25_out, and_27_out);
  not not_15 (not_15_out, Zero);
  and notZero (Overflow, or_5_out, not_15_out);

  assign Negative = MSBout;

  // Other names for the same wires on the sheet: CMD = add0sub1

  // Notes on the sheet:
  //   Add/Sub command
  //   0 add, 1 sub
  //   B Input
  //   L input
  //   A-out output
  //   A Input
  //   Adder
  //   R Input
  //   2's Complement
  //   Status output
  //   -8 + -8 is underflow (not supported)
endmodule

module A5ram (
  input  Clock,
  input  MSBaddy,
  input  in_3,
  input  LSBaddy,
  input  ModeInput,
  input  MSBin,
  input  in_7,
  input  in_8,
  input  LSBin,
  output MSBout,
  output out_11,
  output out_12,
  output LSBout
);

  wire and_1_out, and_2_out, and_3_out, and_4_out, and_5_out, and_6_out, and_7_out, and_8_out, and_9_out,
       and_10_out, and_11_out, and_12_out, and_13_out, and_14_out, and_15_out, and_16_out, and_17_out,
       and_18_out, and_19_out, and_20_out, and_21_out, and_22_out, and_23_out, and_24_out, and_25_out,
       and_26_out, and_27_out, and_28_out, and_29_out, and_30_out, and_31_out, and_32_out, and_33_out,
       and_34_out, and_35_out, and_36_out, and_37_out, and_38_out, and_39_out, and_40_out, and_41_out,
       and_42_out, and_43_out, and_44_out, and_45_out, and_46_out, and_47_out, and_48_out, and_49_out,
       and_50_out, and_51_out, and_52_out, and_53_out, and_54_out, and_55_out, and_56_out, and_57_out,
       and_58_out, and_59_out, and_60_out, and_61_out, and_62_out, and_63_out, and_64_out, and_65_out,
       and_66_out, and_67_out, and_68_out, and_69_out, and_70_out, and_71_out, and_72_out, and_73_out,
       and_74_out, and_75_out, and_76_out, and_77_out, and_78_out, and_79_out, and_80_out, d_ff_1_q,
       d_ff_2_q, d_ff_3_q, d_ff_4_q, d_ff_5_q, d_ff_6_q, d_ff_7_q, d_ff_8_q, d_ff_9_q, d_ff_10_q, d_ff_11_q,
       d_ff_12_q, d_ff_13_q, d_ff_14_q, d_ff_15_q, d_ff_16_q, d_ff_17_q, d_ff_18_q, d_ff_19_q, d_ff_20_q,
       d_ff_21_q, d_ff_22_q, d_ff_23_q, d_ff_25_q, d_ff_29_q, d_ff_30_q, d_ff_31_q, d_ff_32_q, d_ff_33_q,
       d_ff_34_q, d_ff_35_q, d_ff_36_q, d_ff_37_q, d_ff_38_q, d_ff_39_q, d_ff_40_q, d_ff_41_q, d_ff_42_q,
       d_ff_43_q, d_ff_44_q, not_1_out, not_2_out, not_3_out, not_4_out, not_5_out, not_6_out, not_7_out,
       not_8_out, not_9_out, not_10_out, not_11_out, not_12_out, not_13_out, or_1_out, or_2_out, or_3_out,
       or_4_out;

  D_Flip_Flop #(.trigger("falling")) d_ff_1 (.D(MSBaddy), .clk(Clock), .Q(d_ff_1_q));  // open: Qn, preset, reset
  D_Flip_Flop #(.trigger("falling")) d_ff_2 (.D(in_3), .clk(Clock), .Q(d_ff_2_q));  // open: Qn, preset, reset
  not not_1 (not_1_out, d_ff_3_q);
  not not_2 (not_2_out, d_ff_2_q);
  not not_3 (not_3_out, d_ff_2_q);
  not not_4 (not_4_out, d_ff_3_q);
  not not_5 (not_5_out, d_ff_1_q);
  not not_6 (not_6_out, d_ff_1_q);
  not not_7 (not_7_out, d_ff_3_q);
  not not_8 (not_8_out, d_ff_1_q);
  not not_9 (not_9_out, d_ff_2_q);
  not not_10 (not_10_out, d_ff_1_q);
  not not_11 (not_11_out, d_ff_2_q);
  not not_12 (not_12_out, d_ff_3_q);
  D_Flip_Flop #(.trigger("falling")) d_ff_3 (.D(LSBaddy), .clk(Clock), .Q(d_ff_3_q));  // open: Qn, preset, reset
  and and_1 (and_1_out, d_ff_1_q, d_ff_2_q, Clock, d_ff_3_q);
  and and_2 (and_2_out, and_1_out, not_13_out);
  and and_3 (and_3_out, d_ff_1_q, d_ff_2_q, Clock, not_1_out);
  and and_4 (and_4_out, and_3_out, not_13_out);
  and and_5 (and_5_out, d_ff_1_q, not_2_out, Clock, d_ff_3_q);
  and and_6 (and_6_out, and_5_out, not_13_out);
  and and_7 (and_7_out, d_ff_1_q, not_3_out, Clock, not_4_out);
  and and_8 (and_8_out, and_7_out, not_13_out);
  and and_9 (and_9_out, not_5_out, d_ff_2_q, Clock, d_ff_3_q);
  and and_10 (and_10_out, and_9_out, not_13_out);
  and and_11 (and_11_out, not_6_out, d_ff_2_q, Clock, not_7_out);
  and and_12 (and_12_out, and_11_out, not_13_out);
  and and_13 (and_13_out, not_8_out, not_9_out, Clock, d_ff_3_q);
  and and_14 (and_14_out, and_13_out, not_13_out);
  and and_15 (and_15_out, not_10_out, not_11_out, Clock, not_12_out);
  and and_16 (and_16_out, and_15_out, not_13_out);
  D_Flip_Flop #(.trigger("falling")) d_ff_4 (.D(ModeInput), .clk(Clock), .Q(d_ff_4_q));  // open: Qn, preset, reset
  not not_13 (not_13_out, d_ff_4_q);
  and and_17 (and_17_out, and_1_out, not_13_out, d_ff_13_q);
  D_Flip_Flop #(.trigger("high")) d_ff_5 (.D(and_17_out), .clk(and_2_out), .Q(d_ff_5_q));  // open: Qn, preset, reset
  and and_18 (and_18_out, and_3_out, not_13_out, d_ff_13_q);
  D_Flip_Flop #(.trigger("high")) d_ff_6 (.D(and_18_out), .clk(and_4_out), .Q(d_ff_6_q));  // open: Qn, preset, reset
  and and_19 (and_19_out, and_5_out, not_13_out, d_ff_13_q);
  D_Flip_Flop #(.trigger("high")) d_ff_7 (.D(and_19_out), .clk(and_6_out), .Q(d_ff_7_q));  // open: Qn, preset, reset
  and and_20 (and_20_out, and_7_out, not_13_out, d_ff_13_q);
  D_Flip_Flop #(.trigger("high")) d_ff_8 (.D(and_20_out), .clk(and_8_out), .Q(d_ff_8_q));  // open: Qn, preset, reset
  and and_21 (and_21_out, and_9_out, not_13_out, d_ff_13_q);
  D_Flip_Flop #(.trigger("high")) d_ff_9 (.D(and_21_out), .clk(and_10_out), .Q(d_ff_9_q));  // open: Qn, preset, reset
  and and_22 (and_22_out, and_11_out, not_13_out, d_ff_13_q);
  D_Flip_Flop #(.trigger("high")) d_ff_10 (.D(and_22_out), .clk(and_12_out), .Q(d_ff_10_q));  // open: Qn, preset, reset
  and and_23 (and_23_out, and_13_out, not_13_out, d_ff_13_q);
  D_Flip_Flop #(.trigger("high")) d_ff_11 (.D(and_23_out), .clk(and_14_out), .Q(d_ff_11_q));  // open: Qn, preset, reset
  and and_24 (and_24_out, and_15_out, not_13_out, d_ff_13_q);
  D_Flip_Flop #(.trigger("high")) d_ff_12 (.D(and_24_out), .clk(and_16_out), .Q(d_ff_12_q));  // open: Qn, preset, reset
  or or_1 (or_1_out, and_25_out, and_26_out, and_27_out, and_28_out, and_29_out, and_30_out, and_31_out, and_32_out);
  and and_25 (and_25_out, d_ff_5_q, and_1_out, d_ff_4_q);
  and and_26 (and_26_out, d_ff_6_q, and_3_out, d_ff_4_q);
  and and_27 (and_27_out, d_ff_7_q, and_5_out, d_ff_4_q);
  and and_28 (and_28_out, d_ff_8_q, and_7_out, d_ff_4_q);
  and and_29 (and_29_out, d_ff_9_q, and_9_out, d_ff_4_q);
  and and_30 (and_30_out, d_ff_10_q, and_11_out, d_ff_4_q);
  and and_31 (and_31_out, d_ff_11_q, and_13_out, d_ff_4_q);
  and and_32 (and_32_out, d_ff_12_q, and_15_out, d_ff_4_q);
  D_Flip_Flop #(.trigger("falling")) d_ff_13 (.D(MSBin), .clk(Clock), .Q(d_ff_13_q));  // open: Qn, preset, reset
  D_Flip_Flop #(.trigger("falling")) d_ff_14 (.D(in_7), .clk(Clock), .Q(d_ff_14_q));  // open: Qn, preset, reset
  and and_33 (and_33_out, and_1_out, not_13_out, d_ff_14_q);
  D_Flip_Flop #(.trigger("high")) d_ff_15 (.D(and_33_out), .clk(and_2_out), .Q(d_ff_15_q));  // open: Qn, preset, reset
  and and_34 (and_34_out, and_3_out, not_13_out, d_ff_14_q);
  D_Flip_Flop #(.trigger("high")) d_ff_16 (.D(and_34_out), .clk(and_4_out), .Q(d_ff_16_q));  // open: Qn, preset, reset
  and and_35 (and_35_out, and_5_out, not_13_out, d_ff_14_q);
  D_Flip_Flop #(.trigger("high")) d_ff_17 (.D(and_35_out), .clk(and_6_out), .Q(d_ff_17_q));  // open: Qn, preset, reset
  and and_36 (and_36_out, and_7_out, not_13_out, d_ff_14_q);
  D_Flip_Flop #(.trigger("high")) d_ff_18 (.D(and_36_out), .clk(and_8_out), .Q(d_ff_18_q));  // open: Qn, preset, reset
  and and_37 (and_37_out, and_9_out, not_13_out, d_ff_14_q);
  D_Flip_Flop #(.trigger("high")) d_ff_19 (.D(and_37_out), .clk(and_10_out), .Q(d_ff_19_q));  // open: Qn, preset, reset
  and and_38 (and_38_out, and_11_out, not_13_out, d_ff_14_q);
  D_Flip_Flop #(.trigger("high")) d_ff_20 (.D(and_38_out), .clk(and_12_out), .Q(d_ff_20_q));  // open: Qn, preset, reset
  and and_39 (and_39_out, and_13_out, not_13_out, d_ff_14_q);
  D_Flip_Flop #(.trigger("high")) d_ff_21 (.D(and_39_out), .clk(and_14_out), .Q(d_ff_21_q));  // open: Qn, preset, reset
  and and_40 (and_40_out, and_15_out, not_13_out, d_ff_14_q);
  D_Flip_Flop #(.trigger("high")) d_ff_22 (.D(and_40_out), .clk(and_16_out), .Q(d_ff_22_q));  // open: Qn, preset, reset
  D_Flip_Flop #(.trigger("falling")) d_ff_23 (.D(in_8), .clk(Clock), .Q(d_ff_23_q));  // open: Qn, preset, reset
  D_Flip_Flop #(.trigger("high")) d_ff_24 (.D(or_1_out), .clk(Clock), .Q(MSBout));  // open: Qn, preset, reset
  or or_2 (or_2_out, and_41_out, and_42_out, and_43_out, and_44_out, and_45_out, and_46_out, and_47_out, and_48_out);
  and and_41 (and_41_out, d_ff_15_q, and_1_out, d_ff_4_q);
  and and_42 (and_42_out, d_ff_16_q, and_3_out, d_ff_4_q);
  and and_43 (and_43_out, d_ff_17_q, and_5_out, d_ff_4_q);
  and and_44 (and_44_out, d_ff_18_q, and_7_out, d_ff_4_q);
  and and_45 (and_45_out, d_ff_19_q, and_9_out, d_ff_4_q);
  and and_46 (and_46_out, d_ff_20_q, and_11_out, d_ff_4_q);
  and and_47 (and_47_out, d_ff_21_q, and_13_out, d_ff_4_q);
  and and_48 (and_48_out, d_ff_22_q, and_15_out, d_ff_4_q);
  D_Flip_Flop #(.trigger("falling")) d_ff_25 (.D(LSBin), .clk(Clock), .Q(d_ff_25_q));  // open: Qn, preset, reset
  D_Flip_Flop #(.trigger("high")) d_ff_26 (.D(or_2_out), .clk(Clock), .Q(out_11));  // open: Qn, preset, reset
  D_Flip_Flop #(.trigger("high")) d_ff_27 (.D(or_3_out), .clk(Clock), .Q(out_12));  // open: Qn, preset, reset
  and and_49 (and_49_out, and_1_out, not_13_out, d_ff_23_q);
  and and_50 (and_50_out, and_3_out, not_13_out, d_ff_23_q);
  and and_51 (and_51_out, and_5_out, not_13_out, d_ff_23_q);
  and and_52 (and_52_out, and_7_out, not_13_out, d_ff_23_q);
  and and_53 (and_53_out, and_9_out, not_13_out, d_ff_23_q);
  and and_54 (and_54_out, and_11_out, not_13_out, d_ff_23_q);
  and and_55 (and_55_out, and_13_out, not_13_out, d_ff_23_q);
  and and_56 (and_56_out, and_15_out, not_13_out, d_ff_23_q);
  D_Flip_Flop #(.trigger("high")) d_ff_28 (.D(or_4_out), .clk(Clock), .Q(LSBout));  // open: Qn, preset, reset
  D_Flip_Flop #(.trigger("high")) d_ff_29 (.D(and_49_out), .clk(and_2_out), .Q(d_ff_29_q));  // open: Qn, preset, reset
  D_Flip_Flop #(.trigger("high")) d_ff_30 (.D(and_50_out), .clk(and_4_out), .Q(d_ff_30_q));  // open: Qn, preset, reset
  D_Flip_Flop #(.trigger("high")) d_ff_31 (.D(and_51_out), .clk(and_6_out), .Q(d_ff_31_q));  // open: Qn, preset, reset
  D_Flip_Flop #(.trigger("high")) d_ff_32 (.D(and_52_out), .clk(and_8_out), .Q(d_ff_32_q));  // open: Qn, preset, reset
  D_Flip_Flop #(.trigger("high")) d_ff_33 (.D(and_53_out), .clk(and_10_out), .Q(d_ff_33_q));  // open: Qn, preset, reset
  D_Flip_Flop #(.trigger("high")) d_ff_34 (.D(and_54_out), .clk(and_12_out), .Q(d_ff_34_q));  // open: Qn, preset, reset
  D_Flip_Flop #(.trigger("high")) d_ff_35 (.D(and_55_out), .clk(and_14_out), .Q(d_ff_35_q));  // open: Qn, preset, reset
  D_Flip_Flop #(.trigger("high")) d_ff_36 (.D(and_56_out), .clk(and_16_out), .Q(d_ff_36_q));  // open: Qn, preset, reset
  or or_3 (or_3_out, and_57_out, and_58_out, and_59_out, and_60_out, and_61_out, and_62_out, and_63_out, and_64_out);
  and and_57 (and_57_out, d_ff_29_q, and_1_out, d_ff_4_q);
  and and_58 (and_58_out, d_ff_30_q, and_3_out, d_ff_4_q);
  and and_59 (and_59_out, d_ff_31_q, and_5_out, d_ff_4_q);
  and and_60 (and_60_out, d_ff_32_q, and_7_out, d_ff_4_q);
  and and_61 (and_61_out, d_ff_33_q, and_9_out, d_ff_4_q);
  and and_62 (and_62_out, d_ff_34_q, and_11_out, d_ff_4_q);
  and and_63 (and_63_out, d_ff_35_q, and_13_out, d_ff_4_q);
  and and_64 (and_64_out, d_ff_36_q, and_15_out, d_ff_4_q);
  and and_65 (and_65_out, and_1_out, not_13_out, d_ff_25_q);
  D_Flip_Flop #(.trigger("high")) d_ff_37 (.D(and_65_out), .clk(and_2_out), .Q(d_ff_37_q));  // open: Qn, preset, reset
  and and_66 (and_66_out, and_3_out, not_13_out, d_ff_25_q);
  D_Flip_Flop #(.trigger("high")) d_ff_38 (.D(and_66_out), .clk(and_4_out), .Q(d_ff_38_q));  // open: Qn, preset, reset
  and and_67 (and_67_out, and_5_out, not_13_out, d_ff_25_q);
  D_Flip_Flop #(.trigger("high")) d_ff_39 (.D(and_67_out), .clk(and_6_out), .Q(d_ff_39_q));  // open: Qn, preset, reset
  and and_68 (and_68_out, and_7_out, not_13_out, d_ff_25_q);
  D_Flip_Flop #(.trigger("high")) d_ff_40 (.D(and_68_out), .clk(and_8_out), .Q(d_ff_40_q));  // open: Qn, preset, reset
  and and_69 (and_69_out, and_9_out, not_13_out, d_ff_25_q);
  D_Flip_Flop #(.trigger("high")) d_ff_41 (.D(and_69_out), .clk(and_10_out), .Q(d_ff_41_q));  // open: Qn, preset, reset
  and and_70 (and_70_out, and_11_out, not_13_out, d_ff_25_q);
  D_Flip_Flop #(.trigger("high")) d_ff_42 (.D(and_70_out), .clk(and_12_out), .Q(d_ff_42_q));  // open: Qn, preset, reset
  and and_71 (and_71_out, and_13_out, not_13_out, d_ff_25_q);
  D_Flip_Flop #(.trigger("high")) d_ff_43 (.D(and_71_out), .clk(and_14_out), .Q(d_ff_43_q));  // open: Qn, preset, reset
  and and_72 (and_72_out, and_15_out, not_13_out, d_ff_25_q);
  D_Flip_Flop #(.trigger("high")) d_ff_44 (.D(and_72_out), .clk(and_16_out), .Q(d_ff_44_q));  // open: Qn, preset, reset
  or or_4 (or_4_out, and_73_out, and_74_out, and_75_out, and_76_out, and_77_out, and_78_out, and_79_out, and_80_out);
  and and_73 (and_73_out, d_ff_37_q, and_1_out, d_ff_4_q);
  and and_74 (and_74_out, d_ff_38_q, and_3_out, d_ff_4_q);
  and and_75 (and_75_out, d_ff_39_q, and_5_out, d_ff_4_q);
  and and_76 (and_76_out, d_ff_40_q, and_7_out, d_ff_4_q);
  and and_77 (and_77_out, d_ff_41_q, and_9_out, d_ff_4_q);
  and and_78 (and_78_out, d_ff_42_q, and_11_out, d_ff_4_q);
  and and_79 (and_79_out, d_ff_43_q, and_13_out, d_ff_4_q);
  and and_80 (and_80_out, d_ff_44_q, and_15_out, d_ff_4_q);

  // Notes on the sheet:
  //   3-bit address input pins
  //   Mode input pin
  //   4-bit data input pins
  //   4-bit data output pins
endmodule

module A6adder (
  input  A,
  input  B,
  input  Carry,
  output C,
  output Sum
);

  wire and_1_out, and_2_out, xor_1_out;

  and and_1 (and_1_out, A, B);
  xor xor_1 (xor_1_out, A, B);
  and and_2 (and_2_out, xor_1_out, Carry);
  or or_1 (C, and_1_out, and_2_out);
  xor xor_2 (Sum, xor_1_out, Carry);
endmodule

module HalfAdder (
  input  CarryIn,
  input  Input1,
  input  Input2,
  output Sum,
  output CarryOut
);

  wire and_1_out, and_2_out, xor_1_out;

  xor xor_1 (xor_1_out, Input1, Input2);
  and and_1 (and_1_out, CarryIn, xor_1_out);
  and and_2 (and_2_out, Input2, Input1);
  xor xor_2 (Sum, xor_1_out, CarryIn);
  or or_1 (CarryOut, and_1_out, and_2_out);

  // Notes on the sheet:
  //   CarryIn
  //   1
  //   2
  //   Sum
  //   CarryO
endmodule

module README (
);


  // Notes on the sheet:
  //   In case of any confusion with the circuit please email liurui or Alex 
  //   The circuit instruction RAM should ALWAYS be kept on a Read state (1) so that the instructions can propagate into the circuit.
  //   The circuit runs on a clock that propagates on a 2 tick basis. The adder has an initial buffer of 2 ticks for your instructions to be read/written.
  //   All data should be directly inputed into the FlipFlops and all data registers should be on a write state by default as once instructions flow through gates should change back and the inputed data will not be wiped to 0 
  //   In the event that a double add/sub instruction is ran one after the other, the register used to not save the data will automatically read(exit the data) back into the circuit as there is no toggle to prevent data exit.
  //   Note that the use of the input pins for the initial ram SHOULD NOT be used and was only added for testing purposes. The Instruction DATA should always be written using the D-FlipFlops found in each item's sub-circuit file in the Simulate TAB.
endmodule
